// Logisim project ex_4_graph.circ as structural Verilog: 1 circuit, main circuit main
module main (
  input  I0,
  input  I1,
  input  I2,
  output res
);

  wire and_1_out, and_2_out, not_1_out, not_2_out, or_1_out;

  not not_1 (not_1_out, I0);
  not not_2 (not_2_out, I1);
  and and_1 (and_1_out, not_1_out, I1);
  and and_2 (and_2_out, I0, not_2_out);
  or or_1 (or_1_out, and_1_out, and_2_out);
  xor xor_1 (res, or_1_out, I2);
endmodule
