// Logisim project 4to16decoder.circ as structural Verilog: 3 circuits, main circuit fourToSixteenDecoder
module fourToSixteenDecoder (
  input  A3,
  input  A2,
  input  A1,
  input  A0,
  output [7:0] from15to8,
  output [7:0] from7to0
);

  D_74LS138 d_74ls138_1 (.A(A0), .B(A1), .C(A2), .G(1'b1), .G2A(A3), .G2B(1'b0), .Y(from7to0));
  D_74LS138 d_74ls138_2 (.A(A0), .B(A1), .C(A2), .G(A3), .G2A(1'b0), .G2B(1'b0), .Y(from15to8));
endmodule

module D_74LS138 (
  input  A,
  input  B,
  input  C,
  input  G,
  input  G2A,
  input  G2B,
  output [7:0] Y
);

  wire and_1_out, and_2_out, and_3_out, and_4_out, nor_1_out, not_1_out, not_2_out, not_3_out, not_4_out;

  not not_1 (not_1_out, A);
  not not_2 (not_2_out, B);
  not not_3 (not_3_out, G);
  nor nor_1 (nor_1_out, not_3_out, G2A, G2B);
  and and_1 (and_1_out, not_1_out, not_2_out);
  and and_2 (and_2_out, A, not_2_out);
  and and_3 (and_3_out, not_1_out, B);
  and and_4 (and_4_out, A, B);
  not not_4 (not_4_out, C);
  nand nand_1 (Y[0], and_1_out, not_4_out, nor_1_out);
  nand nand_2 (Y[1], and_2_out, not_4_out, nor_1_out);
  nand nand_3 (Y[2], and_3_out, not_4_out, nor_1_out);
  nand nand_4 (Y[3], and_4_out, not_4_out, nor_1_out);
  nand nand_5 (Y[4], and_1_out, C, nor_1_out);
  nand nand_6 (Y[5], and_2_out, C, nor_1_out);
  nand nand_7 (Y[6], and_3_out, C, nor_1_out);
  nand nand_8 (Y[7], and_4_out, C, nor_1_out);
endmodule

module application (
  input  I0,
  input  I1,
  input  I2,
  output res
);

  wire [7:0] m0_y;

  D_74LS138 m0 (.A(I0), .B(I1), .C(I2), .G(1'b1), .G2A(1'b0), .G2B(1'b0), .Y(m0_y));
  nand nand_1 (res, m0_y[0], m0_y[2], m0_y[4], m0_y[5], m0_y[6], m0_y[7]);
endmodule
