// Logisim project DisplaySync.circ as structural Verilog: 3 circuits, main circuit DisplaySync
module DisplaySync (
  input  [1:0] scan,
  input  [15:0] hexs,
  input  [3:0] points,
  input  [3:0] LEs,
  output [3:0] HEX,
  output point,
  output LE,
  output [3:0] AN
);

  Mux4to1b4 mux_hexs (.S(scan), .D0(hexs[3:0]), .D1(hexs[7:4]), .D2(hexs[11:8]), .D3(hexs[15:12]), .Y(HEX));
  Mux4to1 mux_points (.S(scan), .D0(points[0]), .D1(points[1]), .D2(points[2]), .D3(points[3]), .Y(point));
  Mux4to1 mux_LE (.S(scan), .D0(LEs[0]), .D1(LEs[1]), .D2(LEs[2]), .D3(LEs[3]), .Y(LE));
  Mux4to1b4 mux_AN (.S(scan), .D0(4'b1110), .D1(4'b1101), .D2(4'b1011), .D3(4'b0111), .Y(AN));
endmodule

module Mux4to1 (
  input  [1:0] S,
  input  D0,
  input  D1,
  input  D2,
  input  D3,
  output Y
);

  wire and_1_out, and_2_out, and_3_out, and_4_out, and_5_out, and_6_out, and_7_out, and_8_out, not_1_out,
       not_2_out;

  not not_1 (not_1_out, S[0]);
  not not_2 (not_2_out, S[1]);
  and and_1 (and_1_out, not_1_out, not_2_out);
  and and_2 (and_2_out, S[0], not_2_out);
  and and_3 (and_3_out, not_1_out, S[1]);
  and and_4 (and_4_out, S[0], S[1]);
  and and_5 (and_5_out, and_1_out, D0);
  and and_6 (and_6_out, and_2_out, D1);
  and and_7 (and_7_out, and_3_out, D2);
  and and_8 (and_8_out, and_4_out, D3);
  or or_1 (Y, and_5_out, and_6_out, and_7_out, and_8_out);
endmodule

module Mux4to1b4 (
  input  [1:0] S,
  input  [3:0] D0,
  input  [3:0] D1,
  input  [3:0] D2,
  input  [3:0] D3,
  output [3:0] Y
);

  wire and_1_out, and_2_out, and_3_out, and_4_out, and_5_out, and_6_out, and_7_out, and_8_out, and_9_out,
       and_10_out, and_11_out, and_12_out, and_13_out, and_14_out, and_15_out, and_16_out, and_17_out,
       and_18_out, and_19_out, and_20_out, not_1_out, not_2_out;

  not not_1 (not_1_out, S[0]);
  not not_2 (not_2_out, S[1]);
  and and_1 (and_1_out, not_1_out, not_2_out);
  and and_2 (and_2_out, S[0], not_2_out);
  and and_3 (and_3_out, not_1_out, S[1]);
  and and_4 (and_4_out, S[0], S[1]);
  and and_5 (and_5_out, and_1_out, D0[0]);
  and and_6 (and_6_out, and_2_out, D1[0]);
  and and_7 (and_7_out, and_3_out, D2[0]);
  and and_8 (and_8_out, and_4_out, D3[0]);
  and and_9 (and_9_out, and_1_out, D0[1]);
  and and_10 (and_10_out, and_2_out, D1[1]);
  and and_11 (and_11_out, and_3_out, D2[1]);
  and and_12 (and_12_out, and_4_out, D3[1]);
  and and_13 (and_13_out, and_1_out, D0[2]);
  and and_14 (and_14_out, and_2_out, D1[2]);
  and and_15 (and_15_out, and_3_out, D2[2]);
  and and_16 (and_16_out, and_4_out, D3[2]);
  and and_17 (and_17_out, and_1_out, D0[3]);
  and and_18 (and_18_out, and_2_out, D1[3]);
  and and_19 (and_19_out, and_3_out, D2[3]);
  and and_20 (and_20_out, and_4_out, D3[3]);
  or or_1 (Y[0], and_5_out, and_6_out, and_7_out, and_8_out);
  or or_2 (Y[1], and_9_out, and_10_out, and_11_out, and_12_out);
  or or_3 (Y[2], and_13_out, and_14_out, and_15_out, and_16_out);
  or or_4 (Y[3], and_17_out, and_18_out, and_19_out, and_20_out);
endmodule
