// Logisim project MyMC14495.circ as structural Verilog: 1 circuit, main circuit MyMC14495
module MyMC14495 (
  input  D0,
  input  D1,
  input  D2,
  input  D3,
  input  LE,
  input  point,
  output p,
  output a,
  output b,
  output c,
  output d,
  output e,
  output f,
  output g
);

  wire and_1_out, and_2_out, and_3_out, and_4_out, and_5_out, and_6_out, and_7_out, and_8_out, and_9_out,
       and_10_out, and_11_out, and_12_out, and_13_out, and_14_out, and_15_out, and_16_out, and_17_out,
       and_18_out, and_19_out, and_20_out, and_21_out, and_22_out, and_23_out, and_24_out, and_25_out,
       not_2_out, not_3_out, not_4_out, not_5_out, or_1_out, or_3_out, or_5_out, or_8_out, or_9_out,
       or_11_out, or_13_out;

  not not_1 (p, point);
  not not_2 (not_2_out, D0);
  not not_3 (not_3_out, D1);
  not not_4 (not_4_out, D2);
  not not_5 (not_5_out, D3);
  and and_1 (and_1_out, not_5_out, not_4_out, not_3_out, D0);
  and and_2 (and_2_out, not_5_out, D2, not_3_out, not_2_out);
  or or_1 (or_1_out, and_1_out, and_2_out, and_3_out, and_4_out);
  or or_2 (a, LE, or_1_out);
  and and_3 (and_3_out, D3, not_4_out, D1, D0);
  and and_4 (and_4_out, D3, D2, not_3_out, D0);
  and and_5 (and_5_out, D3, D1, D0);
  and and_6 (and_6_out, D2, D1, not_2_out);
  and and_7 (and_7_out, D3, D2, not_2_out);
  or or_3 (or_3_out, and_5_out, and_6_out, and_7_out, and_8_out);
  or or_4 (b, LE, or_3_out);
  and and_8 (and_8_out, not_5_out, D2, not_3_out, D0);
  and and_9 (and_9_out, not_5_out, not_4_out, D1, not_2_out);
  and and_10 (and_10_out, D3, D2, not_2_out);
  or or_5 (or_5_out, and_9_out, and_10_out, and_11_out);
  or or_6 (c, LE, or_5_out);
  and and_11 (and_11_out, D3, D2, D1);
  and and_12 (and_12_out, not_5_out, not_4_out, not_3_out, D0);
  and and_13 (and_13_out, not_5_out, D2, not_3_out, not_2_out);
  or or_7 (d, LE, or_8_out);
  and and_14 (and_14_out, D3, not_4_out, D1, not_2_out);
  or or_8 (or_8_out, and_12_out, and_13_out, and_14_out, and_15_out);
  and and_15 (and_15_out, D2, D1, D0);
  and and_16 (and_16_out, not_5_out, D0);
  and and_17 (and_17_out, not_5_out, D2, not_3_out);
  or or_9 (or_9_out, and_16_out, and_17_out, and_18_out);
  or or_10 (e, LE, or_9_out);
  and and_18 (and_18_out, not_4_out, not_3_out, D0);
  and and_19 (and_19_out, not_5_out, not_4_out, D0);
  and and_20 (and_20_out, not_5_out, not_4_out, D1);
  or or_11 (or_11_out, and_19_out, and_20_out, and_21_out, and_22_out);
  or or_12 (f, LE, or_11_out);
  and and_21 (and_21_out, not_5_out, D1, D0);
  and and_22 (and_22_out, D3, D2, not_3_out, D0);
  and and_23 (and_23_out, not_5_out, not_4_out, not_3_out);
  and and_24 (and_24_out, not_5_out, D2, D1, D0);
  or or_13 (or_13_out, and_23_out, and_24_out, and_25_out);
  or or_14 (g, LE, or_13_out);
  and and_25 (and_25_out, D3, D2, not_3_out, not_2_out);
endmodule
