// Logisim project ALU.circ as structural Verilog: 7 circuits, main circuit ALU
module ALU (
  input  [3:0] A,
  input  [3:0] B,
  input  [1:0] op,
  output [3:0] res,
  output Cout
);

  wire AddSub4b_inst_cout;
  wire [3:0] AddSub4b_inst_s, And2b4_inst_res, Or2b4_inst_res;

  AddSub4b AddSub4b_inst (.A(A), .B(B), .Ctrl(op[0]), .S(AddSub4b_inst_s), .Cout(AddSub4b_inst_cout));
  And2b4 And2b4_inst (.A(A), .B(B), .res(And2b4_inst_res));
  Or2b4 Or2b4_inst (.A(A), .B(B), .res(Or2b4_inst_res));
  Mux4to1b4 Mux4to1b4_inst (
    .S(op), .D0(AddSub4b_inst_s), .D1(AddSub4b_inst_s), .D2(And2b4_inst_res), .D3(Or2b4_inst_res), .Y(res));
  Mux4to1 Mux4to1_inst (.S(op), .D0(AddSub4b_inst_cout), .D1(AddSub4b_inst_cout), .D2(1'b0), .D3(1'b0), .Y(Cout));
endmodule

module AddSub4b (
  input  [3:0] A,
  input  [3:0] B,
  input  Ctrl,
  output [3:0] S,
  output Cout
);

  wire Adder1_inst_cout, Adder2_inst_cout, Adder3_inst_cout, Adder4_inst_cout, xor_1_out, xor_2_out,
       xor_3_out, xor_4_out;

  xor xor_1 (xor_1_out, B[0], Ctrl);
  xor xor_2 (xor_2_out, B[1], Ctrl);
  xor xor_3 (xor_3_out, B[2], Ctrl);
  xor xor_4 (xor_4_out, B[3], Ctrl);
  Adder1b Adder1_inst (.A(A[0]), .B(xor_1_out), .Cin(Ctrl), .S(S[0]), .Cout(Adder1_inst_cout));
  Adder1b Adder2_inst (.A(A[1]), .B(xor_2_out), .Cin(Adder1_inst_cout), .S(S[1]), .Cout(Adder2_inst_cout));
  Adder1b Adder3_inst (.A(A[2]), .B(xor_3_out), .Cin(Adder2_inst_cout), .S(S[2]), .Cout(Adder3_inst_cout));
  Adder1b Adder4_inst (.A(A[3]), .B(xor_4_out), .Cin(Adder3_inst_cout), .S(S[3]), .Cout(Adder4_inst_cout));
  xor xor_5 (Cout, Adder4_inst_cout, Ctrl);
endmodule

module Adder1b (
  input  A,
  input  B,
  input  Cin,
  output S,
  output Cout
);

  wire and_1_out, and_2_out, and_3_out, xor_1_out;

  xor xor_1 (xor_1_out, A, B);
  and and_1 (and_1_out, A, B);
  and and_2 (and_2_out, B, Cin);
  and and_3 (and_3_out, A, Cin);
  xor xor_2 (S, xor_1_out, Cin);
  ExactlyOne xor_3 (.out(Cout), .in0(and_1_out), .in1(and_2_out), .in2(and_3_out));
endmodule

module And2b4 (
  input  [3:0] A,
  input  [3:0] B,
  output [3:0] res
);

  and and_1 (res[0], A[0], B[0]);
  and and_2 (res[1], A[1], B[1]);
  and and_3 (res[2], A[2], B[2]);
  and and_4 (res[3], A[3], B[3]);
endmodule

module Or2b4 (
  input  [3:0] A,
  input  [3:0] B,
  output [3:0] res
);

  or or_1 (res[0], A[0], B[0]);
  or or_2 (res[1], A[1], B[1]);
  or or_3 (res[2], A[2], B[2]);
  or or_4 (res[3], A[3], B[3]);
endmodule

module Mux4to1b4 (
  input  [1:0] S,
  input  [3:0] D0,
  input  [3:0] D1,
  input  [3:0] D2,
  input  [3:0] D3,
  output [3:0] Y
);

  wire and_1_out, and_2_out, and_3_out, and_4_out, and_5_out, and_6_out, and_7_out, and_8_out, and_9_out,
       and_10_out, and_11_out, and_12_out, and_13_out, and_14_out, and_15_out, and_16_out, and_17_out,
       and_18_out, and_19_out, and_20_out, not_1_out, not_2_out;

  not not_1 (not_1_out, S[0]);
  not not_2 (not_2_out, S[1]);
  and and_1 (and_1_out, not_1_out, not_2_out);
  and and_2 (and_2_out, S[0], not_2_out);
  and and_3 (and_3_out, not_1_out, S[1]);
  and and_4 (and_4_out, S[0], S[1]);
  and and_5 (and_5_out, and_1_out, D0[0]);
  and and_6 (and_6_out, and_2_out, D1[0]);
  and and_7 (and_7_out, and_3_out, D2[0]);
  and and_8 (and_8_out, and_4_out, D3[0]);
  and and_9 (and_9_out, and_1_out, D0[1]);
  and and_10 (and_10_out, and_2_out, D1[1]);
  and and_11 (and_11_out, and_3_out, D2[1]);
  and and_12 (and_12_out, and_4_out, D3[1]);
  and and_13 (and_13_out, and_1_out, D0[2]);
  and and_14 (and_14_out, and_2_out, D1[2]);
  and and_15 (and_15_out, and_3_out, D2[2]);
  and and_16 (and_16_out, and_4_out, D3[2]);
  and and_17 (and_17_out, and_1_out, D0[3]);
  and and_18 (and_18_out, and_2_out, D1[3]);
  and and_19 (and_19_out, and_3_out, D2[3]);
  and and_20 (and_20_out, and_4_out, D3[3]);
  or or_1 (Y[0], and_5_out, and_6_out, and_7_out, and_8_out);
  or or_2 (Y[1], and_9_out, and_10_out, and_11_out, and_12_out);
  or or_3 (Y[2], and_13_out, and_14_out, and_15_out, and_16_out);
  or or_4 (Y[3], and_17_out, and_18_out, and_19_out, and_20_out);
endmodule

module Mux4to1 (
  input  [1:0] S,
  input  D0,
  input  D1,
  input  D2,
  input  D3,
  output Y
);

  wire and_1_out, and_2_out, and_3_out, and_4_out, and_5_out, and_6_out, and_7_out, and_8_out, not_1_out,
       not_2_out;

  not not_1 (not_1_out, S[0]);
  not not_2 (not_2_out, S[1]);
  and and_1 (and_1_out, not_1_out, not_2_out);
  and and_2 (and_2_out, S[0], not_2_out);
  and and_3 (and_3_out, not_1_out, S[1]);
  and and_4 (and_4_out, S[0], S[1]);
  and and_5 (and_5_out, and_1_out, D0);
  and and_6 (and_6_out, and_2_out, D1);
  and and_7 (and_7_out, and_3_out, D2);
  and and_8 (and_8_out, and_4_out, D3);
  or or_1 (Y, and_5_out, and_6_out, and_7_out, and_8_out);
endmodule
