// Logisim project AddSub4b.circ as structural Verilog: 2 circuits, main circuit AddSub4b
module AddSub4b (
  input  [3:0] A,
  input  [3:0] B,
  input  Ctrl,
  output [3:0] S,
  output Cout
);

  wire Adder1_inst_cout, Adder2_inst_cout, Adder3_inst_cout, Adder4_inst_cout, xor_1_out, xor_2_out,
       xor_3_out, xor_4_out;

  xor xor_1 (xor_1_out, B[0], Ctrl);
  xor xor_2 (xor_2_out, B[1], Ctrl);
  xor xor_3 (xor_3_out, B[2], Ctrl);
  xor xor_4 (xor_4_out, B[3], Ctrl);
  Adder1b Adder1_inst (.A(A[0]), .B(xor_1_out), .Cin(Ctrl), .S(S[0]), .Cout(Adder1_inst_cout));
  Adder1b Adder2_inst (.A(A[1]), .B(xor_2_out), .Cin(Adder1_inst_cout), .S(S[1]), .Cout(Adder2_inst_cout));
  Adder1b Adder3_inst (.A(A[2]), .B(xor_3_out), .Cin(Adder2_inst_cout), .S(S[2]), .Cout(Adder3_inst_cout));
  Adder1b Adder4_inst (.A(A[3]), .B(xor_4_out), .Cin(Adder3_inst_cout), .S(S[3]), .Cout(Adder4_inst_cout));
  xor xor_5 (Cout, Adder4_inst_cout, Ctrl);
endmodule

module Adder1b (
  input  A,
  input  B,
  input  Cin,
  output S,
  output Cout
);

  wire and_1_out, and_2_out, and_3_out, xor_1_out;

  xor xor_1 (xor_1_out, A, B);
  and and_1 (and_1_out, A, B);
  and and_2 (and_2_out, B, Cin);
  and and_3 (and_3_out, A, Cin);
  xor xor_2 (S, xor_1_out, Cin);
  ExactlyOne xor_3 (.out(Cout), .in0(and_1_out), .in1(and_2_out), .in2(and_3_out));
endmodule
