// Logisim project Adder1b.circ as structural Verilog: 1 circuit, main circuit Adder1b
module Adder1b (
  input  A,
  input  B,
  input  Cin,
  output S,
  output Cout
);

  wire and_1_out, and_2_out, and_3_out, xor_1_out;

  xor xor_1 (xor_1_out, A, B);
  and and_1 (and_1_out, A, B);
  and and_2 (and_2_out, B, Cin);
  and and_3 (and_3_out, A, Cin);
  xor xor_2 (S, xor_1_out, Cin);
  ExactlyOne xor_3 (.out(Cout), .in0(and_1_out), .in1(and_2_out), .in2(and_3_out));
endmodule
