// Logisim project Or2b4.circ as structural Verilog: 1 circuit, main circuit Or2b4
module Or2b4 (
  input  [3:0] A,
  input  [3:0] B,
  output [3:0] res
);

  or or_1 (res[0], A[0], B[0]);
  or or_2 (res[1], A[1], B[1]);
  or or_3 (res[2], A[2], B[2]);
  or or_4 (res[3], A[3], B[3]);
endmodule
