// Logisim project DMS.circ as structural Verilog: 2 circuits, main circuit main
module main (
  input  D,
  input  clk,
  output Qbar,
  output Q
);

  wire master_latch_q, not_1_out;

  not not_1 (not_1_out, clk);
  GatedDLatch master_latch (.D(D), .C(not_1_out), .Q(master_latch_q));  // open: Qbar
  GatedDLatch slave_latch (.D(master_latch_q), .C(clk), .Qbar(Qbar), .Q(Q));
endmodule

module GatedDLatch (
  input  D,
  input  C,
  output Qbar,
  output Q
);

  wire nand_1_out, nand_2_out, not_1_out;

  not not_1 (not_1_out, D);
  nand nand_1 (nand_1_out, not_1_out, C);
  nand nand_2 (nand_2_out, C, D);
  nand nand_3 (Qbar, nand_1_out, Q);
  nand nand_4 (Q, Qbar, nand_2_out);
endmodule
