// Logisim project EdgeTriggered_flipFlop.circ as structural Verilog: 1 circuit, main circuit main
module main (
  input  clk,
  input  D,
  output Q,
  output Qbar
);

  wire nand_1_out, nand_2_out, nand_3_out, nand_4_out;

  nand nand_1 (nand_1_out, nand_4_out, nand_2_out);
  nand nand_2 (nand_2_out, nand_1_out, clk);
  nand nand_3 (nand_3_out, nand_2_out, clk, nand_4_out);
  nand nand_4 (nand_4_out, nand_3_out, D);
  nand nand_5 (Q, nand_2_out, Qbar);
  nand nand_6 (Qbar, Q, nand_3_out);
endmodule
