// Logisim project GatedDLatch.circ as structural Verilog: 1 circuit, main circuit GatedDLatch
module GatedDLatch (
  input  D,
  input  C,
  output Qbar,
  output Q
);

  wire nand_1_out, nand_2_out, not_1_out;

  not not_1 (not_1_out, D);
  nand nand_1 (nand_1_out, not_1_out, C);
  nand nand_2 (nand_2_out, C, D);
  nand nand_3 (Qbar, nand_1_out, Q);
  nand nand_4 (Q, Qbar, nand_2_out);
endmodule
