// Logisim project GatedSRLatch.circ as structural Verilog: 1 circuit, main circuit main
module main (
  input  R,
  input  C,
  input  S,
  output Qbar,
  output Q
);

  wire nand_1_out, nand_2_out;

  nand nand_1 (nand_1_out, R, C);
  nand nand_2 (nand_2_out, C, S);
  nand nand_3 (Qbar, nand_1_out, Q);
  nand nand_4 (Q, Qbar, nand_2_out);
endmodule
