// Logisim project SRMS.circ as structural Verilog: 1 circuit, main circuit main
module main (
  input  S,
  input  clk,
  input  R,
  output mid_Q,
  output mid_Qbar,
  output Q,
  output Qbar
);

  wire nand_1_out, nand_2_out, nand_5_out, nand_6_out, not_1_out, not_2_out;

  nand nand_1 (nand_1_out, S, clk);
  nand nand_2 (nand_2_out, clk, R);
  nand nand_3 (mid_Q, nand_1_out, mid_Qbar);
  nand nand_4 (mid_Qbar, mid_Q, nand_2_out);
  not not_1 (not_1_out, clk);
  not not_2 (not_2_out, clk);
  nand nand_5 (nand_5_out, mid_Q, not_1_out);
  nand nand_6 (nand_6_out, mid_Qbar, not_2_out);
  nand nand_7 (Q, nand_5_out, Qbar);
  nand nand_8 (Qbar, Q, nand_6_out);
endmodule
