// Logisim project SRNANDLatch.circ as structural Verilog: 1 circuit, main circuit main
module main (
  input  Rn,
  input  Sn,
  output Qbar,
  output Q
);

  nand nand_1 (Qbar, Rn, Q);
  nand nand_2 (Q, Qbar, Sn);
endmodule
